# Fritzing sketch pump scetch (saved by Fritzing 0.9.3b)
breadboards: 1

parts:
  Nano2 = Arduino Nano (Rev3.0)
  R1 = Resistor [tolerance=±5% resistance=220 package=THT]
  Q1 = NPN-Transistor [package="TO92 [THT]"]
  M1 = DC Motor
  D1 = Rectifier Diode [part_number=1N4001 package="300 mil [THT]"]
  RE1 = Rotary Encoder [package=THT]  # not connected

nets:
  N1: Nano2.GND, Q1.E
  N2: Nano2.D3, R1.Pin_1
  N3: Nano2.VIN, M1.pin_2, D1.anode
  N4: R1.Pin_0, Q1.B
  N5: Q1.C, M1.pin_1, D1.cathode

custom parts:
  NPN-Transistor: A standard NPN-transistor
